# Fritzing sketch hardware-diagram (saved by Fritzing 1.0.5)

parts:
  Part1 = Soil Moisture Sensor
  Part2 = Soil Moisture Sensor
  Part3 = Soil Moisture Sensor
  Part4 = Soil Moisture Sensor
  A1 = Werner Rothschopf (modified to ESP32-S3-DevKitC dual USB by vanepp Aug 2024)
  U1 = Module 4 Relais 5V [package="Module 4 Relais 5V"]
  VALVE1 = Plastic Solenoid Valve
  VALVE2 = Plastic Solenoid Valve
  VALVE3 = Plastic Solenoid Valve
  VALVE4 = Plastic Solenoid Valve
  DHT2 = DHT11 Humitidy and Temperature Sensor (3 pins)
  e-radionica_com1 = LM393 LDR breakout [part_number=100027]
  U2 = Module 4 Relais 5V [package="Module 4 Relais 5V"]
  VALVE5 = Plastic Solenoid Valve
  VALVE6 = Plastic Solenoid Valve
  VALVE7 = Plastic Solenoid Valve
  VALVE8 = Plastic Solenoid Valve
  S1 = Round Pushbutton
  Boost_Convertor1 = Boost Convertor [part_number=XL6009E1 package=THT]
  Boost_Convertor2 = Boost Convertor [part_number=XL6009E1 package=THT]
  Boost_Convertor3 = Boost Convertor [part_number=XL6009E1 package=THT]
  DC1 = DC_DC_XL4016 [package=board_screw]
  Q2 = Basic FET P-Channel [package="TO220 [THT]"]
  Q3 = Basic FET P-Channel [package="TO220 [THT]"]
  R1 = Resistor [tolerance=±5% power=0.25W resistance=10k package=THT]
  R2 = Resistor [tolerance=±5% power=0.25W resistance=10k package=THT]
  R3 = Resistor [tolerance=±5% power=0.25W resistance=220 package=THT]
  R4 = Resistor [tolerance=±5% power=0.25W resistance=220 package=THT]
  R5 = Resistor [tolerance=±5% power=0.25W resistance=10k package=THT]

nets:
  VCC: Part1.VCC, Part2.VCC, Part3.VCC, Part4.VCC, A1.Pin_2, U1.VCC, DHT2.Plus, e-radionica_com1.VCC, U2.VCC, Boost_Convertor3.Positive_Output, R5.Pin_0
  GND: Part1.GND, Part2.GND, Part3.GND, Part4.GND, A1.Pin_22, A1.Pin_23, A1.Pin_44, U1.GND, DHT2.Gnd, e-radionica_com1.GND, U2.GND, S1.leg1, Boost_Convertor2.Negative_Output, Boost_Convertor3.Negative_Output, Q2.source, Q3.source, R1.Pin_1, R2.Pin_1
  N1: Part1.SIG, A1.Pin_41
  N2: Part2.SIG, A1.Pin_40
  N3: Part3.SIG, A1.Pin_37
  N4: Part4.SIG, A1.Pin_16
  N5: A1.Pin_4, U2.IN1
  N6: A1.Pin_5, U2.IN2
  N7: A1.Pin_6, U2.IN3
  N8: A1.Pin_7, U2.IN4
  N9: A1.Pin_8, U1.IN1
  N10: A1.Pin_9, U1.IN2
  N11: A1.Pin_10, U1.IN3
  N12: A1.Pin_13, S1.leg0
  N13: A1.Pin_19, DHT2.Signal
  N14: A1.Pin_21, Boost_Convertor2.Positive_Output
  N15: A1.Pin_27, U1.IN4
  N16: A1.Pin_29, R4.Pin_0
  N17: A1.Pin_30, R3.Pin_0
  N18: A1.Pin_36, e-radionica_com1.DO
  N19: U1.K1-NF, U1.K2-NF, U1.K3-NF, U1.K4-NF, U2.K1-NF, U2.K2-NF, U2.K3-NF, U2.K4-NF, Boost_Convertor1.Positive_Input, Boost_Convertor2.Positive_Input, Boost_Convertor3.Positive_Input, DC1.OUT+
  N20: U1.K1-Com, VALVE1.no_name_yet#1
  N21: U1.K2-Com, VALVE2.no_name_yet#1
  N22: U1.K3-Com, VALVE3.no_name_yet#1
  N23: U1.K4-Com, VALVE4.no_name_yet#1
  N24: VALVE1.no_name_yet#2, VALVE2.no_name_yet#2, VALVE3.no_name_yet#2, VALVE4.no_name_yet#2, VALVE5.no_name_yet#2, VALVE6.no_name_yet#2, VALVE7.no_name_yet#2, VALVE8.no_name_yet#2, Boost_Convertor1.Negative_Input, Boost_Convertor2.Negative_Input, Boost_Convertor3.Negative_Input, DC1.OUT-
  N25: U2.K1-Com, VALVE8.no_name_yet#1
  N26: U2.K2-Com, VALVE7.no_name_yet#1
  N27: U2.K3-Com, VALVE6.no_name_yet#1
  N28: U2.K4-Com, VALVE5.no_name_yet#1

notes:
  Security Cam 9V
  12V Output
  IRFZ44N
  5V
  3.3V
  IN

custom parts:
  Werner Rothschopf (modified to ESP32-S3-DevKitC dual USB by vanepp Aug 2024): ESP32-S3 ESP32-S3-DevKitC-1 Dual USB development board Pyboard CircuitPython Micropython wifi BLE5.0 ESP32-S3.
  Module 4 Relais 5V: Module 4 Relais 5V 4x SPD-06VDC-SD-C
  DHT11 Humitidy and Temperature Sensor (3 pins): DHT11 Humidity and Temperature Sensor (3 pins).
  Boost Convertor: DC to DC boost convertor
  DC_DC_XL4016: DC-DC Converter step down voltage regulator XL4016 custom sketch.
